# Fritzing sketch Parola_Double_Height_v2 (saved by Fritzing 0.9.4)
breadboards: 3

parts:
  U1 = ESP8266 NodeMCU LoLin module
  Mod1 = MAX7219 8x8 LedMatrix Module
  Part1 = TXB0108 8-channel Bi-directional Logic Level Converter
  Mod2 = MAX7219 8x8 LedMatrix Module

nets:
  N1: U1.3V3, U1.A0, Part1.OE, Part1.VCCA
  GND: U1.GND, Mod1.GND, Part1.GND, Mod2.GND
  N2: U1.D5, Part1.A1
  N3: U1.D7, Part1.A2
  N4: U1.D8, Part1.A3
  N5: Mod1.CLK, Part1.B1, Mod2.CLK
  N6: Mod1.CS, Part1.B3, Mod2.CS
  N7: Mod1.DIN, Part1.B2
  VCC: Mod1.VCC, Part1.VCCB, Mod2.VCC
  N8: Mod1.DOUT, Mod2.DIN

notes:
  40pcs daisy chained
  in two rows (upper,lower) 2 x 20.
  5V 5A rail
  800ma 3.3v rail

custom parts:
  ESP8266 NodeMCU LoLin module: ESP8266 based NodeMCU
  MAX7219 8x8 LedMatrix Module: Description: MAX7219 8x8 LedMatrix Red Module Dimensions: 32x32mm Documents:
  TXB0108 8-channel Bi-directional Logic Level Converter: Because the Arduino (and Basic Stamp) are 5V devices, and most modern sensors, displays, flash cards and modes are 3.3V-only, many makers find that they need to perform level shifting/conversion to protect the 3.3V device from 5V. Although one can use resistors to make a divider, for high speed transfers, the resistors can add a lot of slew and cause havoc that is tough to debug. For that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
